// Logisim project 2207062-counter-7-segment-diaplay-dld-lab-updated.circ as structural Verilog: 3 circuits, main circuit main
module main (
);

  wire counter_1_out_1, counter_1_out_2, counter_1_out_3, decoder_1_b_2, decoder_1_d, decoder_1_e,
       decoder_1_f, decoder_1_g, decoder_1_out_4, decoder_1_out_6;

  counter counter_1 (.out_1(counter_1_out_1), .out_2(counter_1_out_2), .out_3(counter_1_out_3));
  decoder decoder_1 (
    .A(counter_1_out_1), .B(counter_1_out_2), .C(counter_1_out_3), .out_4(decoder_1_out_4),
    .b_2(decoder_1_b_2), .out_6(decoder_1_out_6), .d(decoder_1_d), .e(decoder_1_e), .f(decoder_1_f),
    .g(decoder_1_g));
  _7_Segment_Display u_7_segment_display_1 (
    .g(decoder_1_g), .f(decoder_1_f), .a(decoder_1_out_4), .b(decoder_1_b_2), .e(decoder_1_e),
    .d(decoder_1_d), .c(decoder_1_out_6));  // open: dp
endmodule

module counter (
  output out_1,
  output out_2,
  output out_3
);

  wire and_1_out, and_2_out, and_3_out, clock_1_out, not_1_out, not_2_out, not_3_out, not_4_out, not_5_out,
       or_1_out, or_2_out, or_3_out, or_4_out, or_5_out, t_ff_1_q, t_ff_2_q;

  Clock clock_1 (.out(clock_1_out));
  or or_1 (or_1_out, t_ff_1_q, and_2_out);
  T_Flip_Flop t_ff_1 (.clk(clock_1_out), .T(or_1_out), .Q(t_ff_1_q));  // open: Qn, preset, reset, en
  not not_1 (not_1_out, t_ff_1_q);
  and and_1 (and_1_out, not_1_out, not_3_out, out_2);
  T_Flip_Flop t_ff_2 (.clk(clock_1_out), .T(or_2_out), .Q(t_ff_2_q));  // open: Qn, preset, reset, en
  or or_2 (or_2_out, and_1_out, t_ff_2_q, out_3);
  or or_3 (or_3_out, out_1, not_4_out);
  not not_2 (not_2_out, t_ff_2_q);
  and and_2 (and_2_out, out_1, not_5_out);
  T_Flip_Flop t_ff_3 (.clk(clock_1_out), .T(or_3_out), .Q(out_1));  // open: Qn, preset, reset, en
  not not_3 (not_3_out, out_1);
  LED led_1 (.in(out_1));
  LED led_2 (.in(out_2));
  or or_4 (or_4_out, t_ff_2_q, not_4_out, out_3);
  T_Flip_Flop t_ff_4 (.clk(clock_1_out), .T(or_4_out), .Q(out_2));  // open: Qn, preset, reset, en
  not not_4 (not_4_out, out_2);
  or or_5 (or_5_out, out_3, and_3_out);
  LED led_3 (.in(out_3));
  T_Flip_Flop t_ff_5 (.clk(clock_1_out), .T(or_5_out), .Q(out_3));  // open: Qn, preset, reset, en
  not not_5 (not_5_out, out_3);
  and and_3 (and_3_out, not_4_out, not_2_out);

  // Notes on the sheet:
  //   A
  //   2207062
  //   B
  //   C
  //   D
  //   E
endmodule

module decoder (
  input  A,
  input  B,
  input  C,
  output out_4,
  output b_2,
  output out_6,
  output d,
  output e,
  output f,
  output g
);

  wire and_1_out, and_2_out, and_3_out, and_4_out, and_5_out, and_6_out, and_7_out, and_8_out, and_9_out,
       and_10_out, and_11_out, not_1_out, not_2_out, not_3_out, not_4_out;

  not not_1 (not_1_out, A);
  not not_2 (not_2_out, B);
  not not_3 (not_3_out, C);
  not not_4 (not_4_out, A);
  and and_1 (and_1_out, not_1_out, B);
  and and_2 (and_2_out, not_3_out, B);
  and and_3 (and_3_out, not_1_out, not_3_out);
  and and_4 (and_4_out, A, C);
  and and_5 (and_5_out, C, B);
  or or_1 (out_6, A, not_2_out, C);
  or or_2 (out_4, and_3_out, B, and_4_out);
  and and_6 (and_6_out, not_2_out, not_3_out);
  and and_7 (and_7_out, not_2_out, A);
  and and_8 (and_8_out, B, not_4_out);
  or or_3 (b_2, and_6_out, not_1_out, and_5_out);
  or or_4 (e, and_3_out, and_2_out);
  and and_9 (and_9_out, not_3_out, not_2_out);
  and and_10 (and_10_out, A, not_3_out);
  and and_11 (and_11_out, and_7_out, C);
  or or_5 (g, and_2_out, and_7_out, and_8_out);
  or or_6 (f, and_7_out, and_9_out, and_10_out);
  or or_7 (d, and_3_out, and_1_out, and_2_out, and_11_out);
  _7_Segment_Display u_7_segment_display_1 (.g(g), .f(f), .a(out_4), .b(b_2), .e(e), .d(d), .c(out_6));  // open: dp

  // Notes on the sheet:
  //   BC'
  //   A'C'
  //   A'C'
  //   AB'
  //   c
  //   a
  //   2207062
endmodule
